// Logisim project 16bit_ALU.circ as structural Verilog: 16 circuits, main circuit main
module main (
  input  [15:0] A,
  input  [15:0] B,
  input  [2:0] Select_Operation,
  input  Reset,
  output Overflow,
  output [15:0] Output,
  output Equal,
  output GreaterThan,
  output LessThan
);

  _16bit_ALU ALU (
    .A(A), .Reset(Reset), .B(B), .Operation(Select_Operation), .Overflow(Overflow), .Output(Output),
    .Equal(Equal), .Greater_Than(GreaterThan), .LessThan(LessThan));

  // Notes on the sheet:
  //   MAHARSHI VSHVANATHBHAI BHUVA
  //   AU2540017
  //   MINI PROJECT : ALU DESIGN
  //   SELECT : OPERATIONS
  //   000 ADD
  //   001 SUB
  //   010 AND
  //   011 OR  
  //   100 COM
  //   101 XOR
  //   110 NOT
  //   111 INC
  //   CSE213:DIGITAL LOGIC WITH HARDWARE DESCREPTION LANGUAGE-SECTION:01 | HARMEET KAUR
  //   (A=B)
  //   (A>B)
  //   (A<B)
endmodule

module FullAdder (
  input  A,
  input  B,
  input  Cin,
  output Sum,
  output Cout
);

  wire and_1_out, and_2_out, xor_1_out;

  xor xor_1 (xor_1_out, A, B);
  xor xor_2 (Sum, xor_1_out, Cin);
  and and_1 (and_1_out, Cin, xor_1_out);
  and and_2 (and_2_out, A, B);
  or or_1 (Cout, and_1_out, and_2_out);
endmodule

module Adder4 (
  input  Cin,
  input  [3:0] A,
  input  [3:0] B,
  output [3:0] Sum,
  output Cout
);

  wire fa1_cout, fa2_cout, fa3_cout;

  FullAdder fa1 (.A(A[0]), .B(B[0]), .Cin(Cin), .Sum(Sum[0]), .Cout(fa1_cout));
  FullAdder fa2 (.A(A[1]), .B(B[1]), .Cin(fa1_cout), .Sum(Sum[1]), .Cout(fa2_cout));
  FullAdder fa3 (.A(A[2]), .B(B[2]), .Cin(fa2_cout), .Sum(Sum[2]), .Cout(fa3_cout));
  FullAdder fa4 (.A(A[3]), .B(B[3]), .Cin(fa3_cout), .Sum(Sum[3]), .Cout(Cout));
endmodule

module Adder16 (
  input  Cin,
  input  [15:0] A,
  input  [15:0] B,
  output [15:0] Sum,
  output Cout
);

  wire adder4_1_cout, adder4_2_cout, adder4_3_cout;

  Adder4 adder4_1 (.Cin(Cin), .A(A[3:0]), .B(B[3:0]), .Sum(Sum[3:0]), .Cout(adder4_1_cout));
  Adder4 adder4_2 (.Cin(adder4_1_cout), .A(A[7:4]), .B(B[7:4]), .Sum(Sum[7:4]), .Cout(adder4_2_cout));
  Adder4 adder4_3 (.Cin(adder4_2_cout), .A(A[11:8]), .B(B[11:8]), .Sum(Sum[11:8]), .Cout(adder4_3_cout));
  Adder4 adder4_4 (.Cin(adder4_3_cout), .A(A[15:12]), .B(B[15:12]), .Sum(Sum[15:12]), .Cout(Cout));
endmodule

module FullSubtractor (
  input  A,
  input  B,
  input  Bin,
  output Sum,
  output Bborrow
);

  wire and_1_out, and_2_out, not_1_out, not_2_out, xor_1_out;

  xor xor_1 (xor_1_out, A, B);
  not not_1 (not_1_out, xor_1_out);
  not not_2 (not_2_out, A);
  xor xor_2 (Sum, xor_1_out, Bin);
  and and_1 (and_1_out, not_1_out, Bin);
  and and_2 (and_2_out, not_2_out, B);
  or or_1 (Bborrow, and_1_out, and_2_out);
endmodule

module Subtractor4 (
  input  Bin,
  input  [3:0] A,
  input  [3:0] B,
  output [3:0] Difference,
  output Bout
);

  wire sa1_bborrow, sa2_bborrow, sa3_bborrow;

  FullSubtractor sa1 (.A(A[0]), .B(B[0]), .Bin(Bin), .Sum(Difference[0]), .Bborrow(sa1_bborrow));
  FullSubtractor sa2 (.A(A[1]), .B(B[1]), .Bin(sa1_bborrow), .Sum(Difference[1]), .Bborrow(sa2_bborrow));
  FullSubtractor sa3 (.A(A[2]), .B(B[2]), .Bin(sa2_bborrow), .Sum(Difference[2]), .Bborrow(sa3_bborrow));
  FullSubtractor sa4 (.A(A[3]), .B(B[3]), .Bin(sa3_bborrow), .Sum(Difference[3]), .Bborrow(Bout));
endmodule

module Subtractor16 (
  input  Bin,
  input  [15:0] A,
  input  [15:0] B,
  output [15:0] Difference,
  output Bout
);

  wire sub4_1_bout, sub4_2_bout, sub4_3_bout;

  Subtractor4 sub4_1 (.Bin(Bin), .A(A[3:0]), .B(B[3:0]), .Difference(Difference[3:0]), .Bout(sub4_1_bout));
  Subtractor4 sub4_2 (.Bin(sub4_1_bout), .A(A[7:4]), .B(B[7:4]), .Difference(Difference[7:4]), .Bout(sub4_2_bout));
  Subtractor4 sub4_3 (.Bin(sub4_2_bout), .A(A[11:8]), .B(B[11:8]), .Difference(Difference[11:8]), .Bout(sub4_3_bout));
  Subtractor4 sub4_4 (.Bin(sub4_3_bout), .A(A[15:12]), .B(B[15:12]), .Difference(Difference[15:12]), .Bout(Bout));
endmodule

module AND (
  input  [15:0] A,
  input  [15:0] B,
  output [15:0] Output
);

  assign Output = A & B;  // AND_Gate _16_Bit_AND_Gate, 16 bits wide
endmodule

module OR (
  input  [15:0] A,
  input  [15:0] B,
  output [15:0] Output
);

  assign Output = A | B;  // OR_Gate _16_Bit_OR_Gate, 16 bits wide
endmodule

module XOR (
  input  [15:0] A,
  input  [15:0] B,
  output [15:0] Output
);

  assign Output = A ^ B;  // XOR_Gate _16_Bit_XOR_Gate, 16 bits wide
endmodule

module NOT_A (
  input  [15:0] A,
  output [15:0] Output
);

  assign Output = ~A;  // NOT_Gate not_1, 16 bits wide
endmodule

module NOT_B (
  input  [15:0] B,
  output [15:0] Output
);

  assign Output = ~B;  // NOT_Gate not_1, 16 bits wide
endmodule

module Increment (
  input  [15:0] A,
  output [15:0] Output
);

  Adder16 Adder16 (.Cin(1'b0), .A(A), .B(16'h1), .Sum(Output));  // open: Cout
endmodule

module Compare (
  input  [15:0] A,
  input  [15:0] B,
  output Equal,
  output Greater_Than,
  output out_5
);

  wire or_1_out;
  wire [15:0] Sub_16_difference;

  Subtractor16 Sub_16 (.Bin(1'b0), .A(A), .B(B), .Difference(Sub_16_difference), .Bout(out_5));
  nor nor_1 (Equal, Sub_16_difference[0], Sub_16_difference[1], Sub_16_difference[2], Sub_16_difference[3], Sub_16_difference[4], Sub_16_difference[5], Sub_16_difference[6], Sub_16_difference[7], Sub_16_difference[8], Sub_16_difference[9], Sub_16_difference[10], Sub_16_difference[11], Sub_16_difference[12], Sub_16_difference[13], Sub_16_difference[14], Sub_16_difference[15]);
  or or_1 (or_1_out, Equal, out_5);
  not not_1 (Greater_Than, or_1_out);
endmodule

module Overflow (
  input  [15:0] A,
  input  [15:0] B,
  input  [15:0] Sum,
  output Overflow
);

  wire not_1_out, xor_1_out, xor_2_out;

  not not_1 (not_1_out, xor_1_out);
  xor xor_1 (xor_1_out, A[15], B[15]);
  xor xor_2 (xor_2_out, A[15], Sum[15]);
  and and_1 (Overflow, not_1_out, xor_2_out);
endmodule

module _16bit_ALU (
  input  [15:0] A,
  input  Reset,
  input  [15:0] B,
  input  [2:0] Operation,
  output Overflow,
  output [15:0] Output,
  output Equal,
  output Greater_Than,
  output LessThan
);

  wire _16BitCompare_equal, _16BitCompare_greater_than, _16BitCompare_out_5, and_1_out;
  wire [15:0] _16BitAdder_sum, _16BitAND_output, _16BitIncrementer_output, _16BitOR_output,
       _16BitSubtractor_difference, _16BitXOR_output, multiplexer_1_out, NOT_A_output;

  Overflow _16BitOverflow (.A(A), .B(B), .Sum(_16BitAdder_sum), .Overflow(Overflow));
  Adder16 _16BitAdder (.Cin(1'b0), .A(A), .B(B), .Sum(_16BitAdder_sum));  // open: Cout
  Subtractor16 _16BitSubtractor (.Bin(1'b0), .A(A), .B(B), .Difference(_16BitSubtractor_difference));  // open: Bout
  AND _16BitAND (.A(A), .B(B), .Output(_16BitAND_output));
  OR _16BitOR (.A(A), .B(B), .Output(_16BitOR_output));
  XOR _16BitXOR (.A(A), .B(B), .Output(_16BitXOR_output));
  NOT_A NOT_A (.A(A), .Output(NOT_A_output));
  Increment _16BitIncrementer (.A(A), .Output(_16BitIncrementer_output));
  Compare _16BitCompare (
    .A(A), .B(B), .out_5(_16BitCompare_out_5), .Equal(_16BitCompare_equal),
    .Greater_Than(_16BitCompare_greater_than));
  Multiplexer #(.select(3), .width(16)) multiplexer_1 (
    .in0(_16BitAdder_sum), .in1(_16BitSubtractor_difference), .in2(_16BitAND_output), .in3(_16BitOR_output),
    .in4({16{1'b0}}), .in5(_16BitXOR_output), .in6(NOT_A_output), .in7(_16BitIncrementer_output),
    .out(multiplexer_1_out), .sel(Operation));  // open: en
  and and_1 (and_1_out, ~Operation[0], ~Operation[1], Operation[2]);  // AND_Gate
  Multiplexer #(.width(16)) multiplexer_2 (
    .in0(multiplexer_1_out), .in1({16{1'b0}}), .out(Output), .sel(Reset));  // open: en
  and and_2 (Equal, and_1_out, _16BitCompare_equal);
  and and_3 (Greater_Than, and_1_out, _16BitCompare_greater_than);
  and and_4 (LessThan, and_1_out, _16BitCompare_out_5);

  // Notes on the sheet:
  //   (A>B)
  //   (A>B)
  //   (A,B)
endmodule
